// Logisim project 4_bit_mag_comp.circ as structural Verilog: 1 circuit, main circuit main
module main (
  input  A3,
  input  B3,
  input  A2,
  input  B2,
  input  [3:0] A,
  input  A1,
  input  [3:0] B,
  input  B1,
  input  A0,
  input  B0
);

  wire and_1_out, and_2_out, and_3_out, and_4_out, and_5_out, and_6_out, and_7_out, and_8_out, and_9_out,
       and_10_out, and_11_out, and_12_out, and_13_out, and_14_out, and_15_out, and_16_out, and_17_out,
       and_18_out, and_19_out, and_20_out, and_21_out, and_22_out, and_23_out, and_24_out, and_25_out,
       and_26_out, and_27_out, and_28_out, and_29_out, and_30_out, nor_1_out, nor_2_out, nor_3_out,
       nor_4_out, nor_5_out, nor_6_out, nor_7_out, nor_8_out, not_1_out, not_2_out, not_3_out, not_4_out,
       not_5_out, not_6_out, not_7_out, not_8_out, not_9_out, not_10_out, not_11_out, not_12_out, not_13_out,
       not_14_out, not_15_out, not_16_out, or_1_out, or_2_out, or_3_out, or_4_out;

  not not_1 (not_1_out, A[3]);
  not not_2 (not_2_out, B[3]);
  not not_3 (not_3_out, A[2]);
  not not_4 (not_4_out, B[2]);
  not not_5 (not_5_out, A[1]);
  not not_6 (not_6_out, B[1]);
  not not_7 (not_7_out, A[0]);
  not not_8 (not_8_out, B[0]);
  and and_1 (and_1_out, A[3], not_2_out);
  and and_2 (and_2_out, not_1_out, B[3]);
  and and_3 (and_3_out, A[2], not_4_out);
  and and_4 (and_4_out, not_3_out, B[2]);
  and and_5 (and_5_out, A[1], not_6_out);
  and and_6 (and_6_out, not_5_out, B[1]);
  and and_7 (and_7_out, A[0], not_8_out);
  and and_8 (and_8_out, not_7_out, B[0]);
  nor nor_1 (nor_1_out, and_1_out, and_2_out);
  nor nor_2 (nor_2_out, and_3_out, and_4_out);
  nor nor_3 (nor_3_out, and_5_out, and_6_out);
  nor nor_4 (nor_4_out, and_7_out, and_8_out);
  and and_9 (and_9_out, nor_1_out, and_4_out);
  and and_10 (and_10_out, nor_1_out, and_3_out);
  and and_11 (and_11_out, nor_1_out, nor_2_out, and_5_out);
  and and_12 (and_12_out, nor_1_out, nor_2_out, and_6_out);
  and and_13 (and_13_out, and_7_out, nor_1_out, nor_2_out, nor_3_out);
  and and_14 (and_14_out, nor_1_out, nor_2_out, nor_3_out, and_8_out);
  or or_1 (or_1_out, and_1_out, and_10_out, and_11_out, and_13_out);
  and and_15 (and_15_out, nor_1_out, nor_2_out, nor_3_out, nor_4_out);
  or or_2 (or_2_out, and_2_out, and_9_out, and_12_out, and_14_out);
  LED led_1 (.in(or_1_out));
  LED led_2 (.in(and_15_out));
  LED led_3 (.in(or_2_out));
  not not_9 (not_9_out, A3);
  not not_10 (not_10_out, B3);
  not not_11 (not_11_out, A2);
  not not_12 (not_12_out, B2);
  not not_13 (not_13_out, A1);
  not not_14 (not_14_out, B1);
  not not_15 (not_15_out, A0);
  not not_16 (not_16_out, B0);
  and and_16 (and_16_out, A3, not_10_out);
  and and_17 (and_17_out, not_9_out, B3);
  and and_18 (and_18_out, A2, not_12_out);
  and and_19 (and_19_out, not_11_out, B2);
  and and_20 (and_20_out, A1, not_14_out);
  and and_21 (and_21_out, not_13_out, B1);
  and and_22 (and_22_out, A0, not_16_out);
  and and_23 (and_23_out, not_15_out, B0);
  nor nor_5 (nor_5_out, and_16_out, and_17_out);
  nor nor_6 (nor_6_out, and_18_out, and_19_out);
  nor nor_7 (nor_7_out, and_20_out, and_21_out);
  nor nor_8 (nor_8_out, and_22_out, and_23_out);
  and and_24 (and_24_out, nor_5_out, and_19_out);
  and and_25 (and_25_out, nor_5_out, and_18_out);
  and and_26 (and_26_out, nor_5_out, nor_6_out, and_20_out);
  and and_27 (and_27_out, nor_5_out, nor_6_out, and_21_out);
  and and_28 (and_28_out, and_22_out, nor_5_out, nor_6_out, nor_7_out);
  and and_29 (and_29_out, nor_5_out, nor_6_out, nor_7_out, and_23_out);
  or or_3 (or_3_out, and_16_out, and_25_out, and_26_out, and_28_out);
  and and_30 (and_30_out, nor_5_out, nor_6_out, nor_7_out, nor_8_out);
  or or_4 (or_4_out, and_17_out, and_24_out, and_27_out, and_29_out);
  LED led_4 (.in(or_3_out));
  LED led_5 (.in(and_30_out));
  LED led_6 (.in(or_4_out));

  // Notes on the sheet:
  //   A>B
  //   A=B
  //   A<B
  //   A>B
  //   A=B
  //   A<B
endmodule
